# Fritzing sketch scheme (saved by Fritzing 0.9.3b)
breadboards: 1

parts:
  Part1 = Arduino Mega 2560 (Rev3)
  GLCD_128x1 = 128 x 64 Graphic LCD
  U2 = LM3480IM4 [package=sot23-3]

nets:
  N1: Part1.5V, U2.IN
  GND: Part1.GND, GLCD_128x1.20_K(-), U2.GND
  N2: GLCD_128x1.19_A(+), U2.OUT
